// Logisim project projeto.circ as structural Verilog: 2 circuits, main circuit main
module main (
  input  A,
  input  in_2,
  input  in_3,
  input  in_4,
  input  B,
  input  in_6,
  input  in_7,
  input  in_8,
  input  \subtração_1 
);

  wire display_1_a1, display_1_b2, display_1_c2, display_1_d2, display_1_e, display_1_f, display_1_g,
       display_2_a1, display_2_b2, display_2_c2, display_2_d2, display_2_e, display_2_f, display_2_g;
  wire [3:0] adder_1_out, xor_4_out;
  wire [4:4] adder_1_cout;
  wire [8:0] rom_1_data;

  xor xor_1 (xor_4_out[1], \subtração_1 , in_7);
  xor xor_2 (xor_4_out[2], \subtração_1 , in_6);
  xor xor_3 (xor_4_out[3], \subtração_1 , B);
  xor xor_4 (xor_4_out[0], \subtração_1 , in_8);
  Adder #(.width(4)) adder_1 (
    .a({A, in_2, in_3, in_4}), .b(xor_4_out), .out(adder_1_out), .cin(\subtração_1 ), .cout(adder_1_cout[4]));
  ROM #(.addrWidth(9), .dataWidth(9)) rom_1 (
    .addr({3'b000, \subtração_1 , adder_1_cout[4], adder_1_out}), .data(rom_1_data));  // open: sel
  LED led_1 (.in(rom_1_data[5]));
  LED led_2 (.in(rom_1_data[6]));
  LED led_3 (.in(rom_1_data[7]));
  _7_Segment_Display u_7_segment_display_1 (.g(rom_1_data[8]));  // open: f, a, b, e, d, c, dp
  LED led_4 (.in(rom_1_data[2]));
  LED led_5 (.in(rom_1_data[3]));
  LED led_6 (.in(rom_1_data[4]));
  display display_1 (
    .a(rom_1_data[7]), .b(rom_1_data[6]), .c(rom_1_data[5]), .d(rom_1_data[4]), .a1(display_1_a1),
    .b2(display_1_b2), .c2(display_1_c2), .d2(display_1_d2), .e(display_1_e), .f(display_1_f), .g(display_1_g));
  _7_Segment_Display u_7_segment_display_2 (
    .g(display_1_g), .f(display_1_f), .a(display_1_a1), .b(display_1_b2), .e(display_1_e), .d(display_1_d2),
    .c(display_1_c2));  // open: dp
  _7_Segment_Display u_7_segment_display_3 (
    .g(display_2_g), .f(display_2_f), .a(display_2_a1), .b(display_2_b2), .e(display_2_e), .d(display_2_d2),
    .c(display_2_c2));  // open: dp
  LED led_7 (.in(rom_1_data[0]));
  LED led_8 (.in(rom_1_data[1]));
  display display_2 (
    .a(rom_1_data[3]), .b(rom_1_data[2]), .c(rom_1_data[1]), .d(rom_1_data[0]), .a1(display_2_a1),
    .b2(display_2_b2), .c2(display_2_c2), .d2(display_2_d2), .e(display_2_e), .f(display_2_f), .g(display_2_g));

  // Notes on the sheet:
  //   André Gonçalves
  //   Tiago Gonçalves
  //   XOR gates
  //   para abilitar
  //   a subtração
  //   soma = 0
  //   Full adder/sub
  //   de 4 bits
  //   ,em vez de ter
  //   muitos muxes ou
  //   gates, assim 
  //   fica mais simples
  //   de "ler".
  //   Rom para converter binario para decimal
  //   contents of rom_1 (hex, n*v repeats v):
  //   0 1 2 3 4 5 6 7 8 9 10 11 12 13 14 15 16 17 18 19 20 21 22 23 24 25 26 27 28 29 30 31 0 115 114 113
  //   112 111 110 109 108 107 106 105 104 103 102 101 0 1 2 3 4 5 6 7 8 9 10 11 12 13 14 15
  //   Display
  //   do resultado
  //   em decimal
  //   Resultado em dois digitos binarios
  //   Descodificadores
  //   para os displays
endmodule

module display (
  input  a,
  input  b,
  input  c,
  input  d,
  output a1,
  output b2,
  output c2,
  output d2,
  output e,
  output f,
  output g
);

  wire and_1_out, and_2_out, and_3_out, and_4_out, and_5_out, and_6_out, and_7_out, and_8_out, and_9_out,
       and_10_out, and_11_out, and_12_out, and_13_out, and_14_out, and_15_out, and_16_out, and_17_out,
       and_18_out, and_19_out, and_20_out, and_21_out, and_22_out, and_23_out, and_24_out, and_25_out,
       and_26_out, not_1_out, not_2_out, not_3_out, not_4_out, not_5_out, not_6_out, not_7_out, not_8_out,
       not_9_out, not_10_out, not_11_out, not_12_out, not_13_out, not_14_out, not_15_out, not_16_out,
       not_17_out, not_18_out, not_19_out, not_20_out, not_21_out, not_22_out, not_23_out, not_24_out,
       not_25_out, not_26_out, not_27_out, not_28_out, not_29_out, not_30_out, not_31_out, not_32_out,
       not_33_out, not_34_out, not_35_out, not_36_out, not_37_out, not_38_out, not_39_out, not_40_out,
       not_41_out, not_42_out, not_43_out, not_44_out, not_45_out, not_46_out, not_47_out, not_48_out,
       not_49_out, not_50_out, not_51_out, not_52_out;

  not not_1 (not_1_out, a);
  not not_2 (not_2_out, b);
  and and_1 (and_1_out, not_1_out, not_2_out, not_3_out);
  not not_3 (not_3_out, d);
  not not_4 (not_4_out, a);
  and and_2 (and_2_out, not_4_out, c);
  not not_5 (not_5_out, a);
  and and_3 (and_3_out, not_5_out, b, d);
  and and_4 (and_4_out, a, not_6_out, not_7_out);
  not not_6 (not_6_out, b);
  not not_7 (not_7_out, c);
  not not_8 (not_8_out, a);
  and and_5 (and_5_out, not_8_out, not_9_out);
  not not_9 (not_9_out, b);
  not not_10 (not_10_out, a);
  not not_11 (not_11_out, c);
  and and_6 (and_6_out, not_10_out, not_11_out, not_12_out);
  not not_12 (not_12_out, d);
  not not_13 (not_13_out, b);
  and and_7 (and_7_out, not_13_out, not_14_out);
  not not_14 (not_14_out, c);
  not not_15 (not_15_out, a);
  and and_8 (and_8_out, not_15_out, c, d);
  not not_16 (not_16_out, b);
  and and_9 (and_9_out, not_16_out, not_17_out);
  not not_17 (not_17_out, c);
  not not_18 (not_18_out, a);
  and and_10 (and_10_out, not_18_out, d);
  not not_19 (not_19_out, a);
  and and_11 (and_11_out, not_19_out, b);
  not not_20 (not_20_out, a);
  not not_21 (not_21_out, b);
  not not_22 (not_22_out, d);
  not not_23 (not_23_out, a);
  not not_24 (not_24_out, b);
  not not_25 (not_25_out, a);
  not not_26 (not_26_out, d);
  not not_27 (not_27_out, a);
  not not_28 (not_28_out, c);
  not not_29 (not_29_out, b);
  not not_30 (not_30_out, c);
  not not_31 (not_31_out, b);
  not not_32 (not_32_out, c);
  and and_12 (and_12_out, not_31_out, not_32_out, not_33_out);
  not not_33 (not_33_out, d);
  not not_34 (not_34_out, a);
  and and_13 (and_13_out, not_34_out, c, not_35_out);
  not not_35 (not_35_out, d);
  not not_36 (not_36_out, a);
  not not_37 (not_37_out, c);
  and and_14 (and_14_out, not_36_out, not_37_out, not_38_out);
  not not_38 (not_38_out, d);
  not not_39 (not_39_out, a);
  and and_15 (and_15_out, not_39_out, b, not_40_out);
  not not_40 (not_40_out, c);
  not not_41 (not_41_out, a);
  and and_16 (and_16_out, not_41_out, b, not_42_out);
  not not_42 (not_42_out, d);
  and and_17 (and_17_out, a, not_43_out, not_44_out);
  not not_43 (not_43_out, b);
  not not_44 (not_44_out, c);
  not not_45 (not_45_out, a);
  not not_46 (not_46_out, b);
  and and_18 (and_18_out, not_45_out, not_46_out, c);
  not not_47 (not_47_out, a);
  and and_19 (and_19_out, not_47_out, b, not_48_out);
  not not_48 (not_48_out, c);
  not not_49 (not_49_out, a);
  and and_20 (and_20_out, not_49_out, b, not_50_out);
  not not_50 (not_50_out, d);
  not not_51 (not_51_out, b);
  and and_21 (and_21_out, a, not_51_out, not_52_out);
  not not_52 (not_52_out, c);
  or or_1 (a1, and_1_out, and_2_out, and_3_out, and_4_out);
  or or_2 (b2, and_5_out, and_6_out, and_7_out, and_8_out);
  or or_3 (c2, and_9_out, and_10_out, and_11_out);
  and and_22 (and_22_out, not_20_out, not_21_out, not_22_out);
  and and_23 (and_23_out, not_23_out, not_24_out, c);
  and and_24 (and_24_out, not_25_out, c, not_26_out);
  and and_25 (and_25_out, not_27_out, b, not_28_out, d);
  and and_26 (and_26_out, a, not_29_out, not_30_out);
  or or_4 (e, and_12_out, and_13_out);
  or or_5 (f, and_14_out, and_15_out, and_16_out, and_17_out);
  or or_6 (g, and_18_out, and_19_out, and_20_out, and_21_out);
  or or_7 (d2, and_22_out, and_23_out, and_24_out, and_25_out, and_26_out);
endmodule
